# Fritzing sketch Untitled Sketch 2 (saved by Fritzing 0.8.3b)

parts:
  S1 = H-Bridge with L298N
  Part1 = Arduino Uno (Rev3)
  BAT1 = Battery Holders [package=battery-aa]
  M1 = Getriebemotor

nets:
  N1: S1.12V, BAT1.-
  GND: S1.GND, Part1.GND, BAT1.+
  N2: S1.ENA, Part1.D10_PWM/SS
  N3: S1.IN1, Part1.D7
  N4: S1.IN2, Part1.D8
  N5: S1.M1-01, M1.pin_2
  N6: S1.M1-02, M1.pin_1

custom parts:
  H-Bridge with L298N: h-bridge
