# Fritzing sketch Untitled Sketch 3 (saved by Fritzing 0.8.3b)
breadboards: 1

parts:
  S1 = H-Bridge with L298N
  Part1 = Arduino Uno (Rev3)
  BAT1 = Battery Holders [package=battery-aa]
  M1 = Getriebemotor
  D1 = Diode [package=diode-1n4001]
  Q1 = TIP120 Hi-Current Darlington Transistor
  VALVE1 = Plastic Solenoid Valve
  R1 = Resistor [tolerance=±5% resistance=1k package=THT]

nets:
  N1: S1.12V, BAT1.-
  GND: S1.GND, Part1.GND, BAT1.+
  N2: S1.ENA, Part1.D10_PWM/SS
  N3: S1.IN1, Part1.D7
  N4: S1.IN2, Part1.D8
  N5: S1.M1-01, M1.pin_2
  N6: S1.M1-02, M1.pin_1
  N7: S1.M2-01, S1.M2-02
  N8: Part1.D4, R1.Pin_0
  N9: D1.A, VALVE1.no_name_yet#1
  N10: D1.C, VALVE1.no_name_yet#2
  N11: Q1.COLLECTOR, R1.Pin_1

custom parts:
  H-Bridge with L298N: h-bridge
