# Fritzing sketch Untitled Sketch (saved by Fritzing 0.8.3b)
breadboards: 1

parts:
  Part2 = Arduino Uno (Rev3)
  L298N1 = L298N DC motor driver
  M1 = Getriebemotor
  Water_Pressure_Sensor_SEN1 = Gravity: Analog Water Pressure Sensor SEN0257
  BATT1 = LiPoly Battery (1300mAh)

nets:
  N1: Part2.A1, Water_Pressure_Sensor_SEN1.Signal
  GND: Part2.GND, L298N1.GND, Water_Pressure_Sensor_SEN1.GND, BATT1.negative
  N2: Part2.D8, L298N1.IN1
  N3: Part2.D10_PWM/SS, L298N1.5V, L298N1.ENA
  N4: Part2.D7, L298N1.IN2
  5V: Part2.5V, Water_Pressure_Sensor_SEN1.VCC
  N5: L298N1.OUT3, M1.pin_2
  N6: L298N1.OUT4, M1.pin_1
  N7: L298N1.12V, BATT1.positive

custom parts:
  L298N DC motor driver: 2x DC motor driver with 78M05 positive voltage regulator (7..35 V) L298N: max 46 V, 2 A Set 5 V Enable jumper to enable 5 V regultor (needed for the L298N) and +5 V output at screw terminal or supply external +5 V at screw terminal Set ENA and/or ENB to +5 V to enable motor permanently or supply ENA and/or ENB with PWM signal IN1 and IN2 set rotation directory for motor A (OUT1/OUT2) IN2 and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
  LiPoly Battery (1300mAh): Lithium Ion Polymer Battery (1300mAh)

// code stored in the sketch: code.ino
//sudo chmod a+rw /dev/ttyUSB0

//curves
float mat1[2]={1.0 ,12.0},
mat2[2]={1.5, 10.0},
 mat3[2]={2.0, 8.0};

int enA = 10;
int in1 = 8;
int in2 = 7;
int an1 = 1;
int speed = 250;
const float OffSet = 0.483;
float thumbArea = 0.0004;
float currentPresure = 0.0;
float targetPresure = 0.0;
void printMessage(String preMessage, float value, String postMessage);


    void setup()
{


  Serial.begin(9600);
  pinMode(in1, OUTPUT);
  pinMode(in2, OUTPUT);
  pinMode(enA, OUTPUT);
  analogWrite(enA, speed);
}


void loop()
{


  currentPresure = getPresureInPascal();
  //message currentPresure
  printMessage("current Presure", currentPresure, "Pa");


  if (getPresureInPascal() > currentPresure + OffSet)
  {
    //message currentPresure change
    printMessage("Presure change (dif)", getPresureInPascal() - currentPresure, "Pa");
    targetPresure = getTargetPresure(currentPresure, getPresureInPascal(), thumbArea, mat1);
    //message TargetPresure change
    printMessage("Target Presure", targetPresure, "Pa");
    while (targetPresure == getPresureInPascal())


    {
      //message Presure change precentage
      printMessage("Adjusting Presure", (targetPresure - getPresureInPascal()) / (targetPresure - currentPresure), "Pa");
      digitalWrite(in1, HIGH);
      digitalWrite(in2, LOW);
    }
  }
  //message TargetPresure archived
  printMessage("Target Presure archived", targetPresure, "Pa");
  digitalWrite(in1, LOW);
  digitalWrite(in2, LOW);
}


float getPresureInPascal()
{
  int P = ((analogRead(an1) * 5.00 / 1024) - OffSet) * 400;
  return P;
}


float getTargetPresure(float initP, float endP, float thumbArea, float materialCurve[])
{
  //Y=mx+c
  float appliedForce = (endP - initP) * thumbArea;
  if (appliedForce > materialCurve[1])
  {
    appliedForce = materialCurve[1];
  }
  return (endP + appliedForce * materialCurve[0]);
}


void printMessage(String preMessage = "", float value = 0.0, String postMessage = "")
{
  Serial.println("");
  Serial.print(preMessage);
  Serial.print(value);
  Serial.print(" - ");
  Serial.print(postMessage);
  Serial.print(" ");
  Serial.println("");
}

